# Fritzing sketch colour sorter (saved by Fritzing 0.9.3b)
breadboards: 1

parts:
  Part1 = Arduino BT  # not connected
  J1 = Basic Servo
  J2 = Basic Servo
  J3 = Basic Servo
  J4 = Basic Servo
  hc-sr1 = hc-sr04
  e-radionica1 = TCS230 Color Sensor [part_number=101209]
  JACK1 = 2.1mm Barrel Jack with Terminal Block
  Part2 = Arduino Mega 2560 (Rev3)

nets:
  GND: J1.gnd, J2.gnd, J3.gnd, J4.gnd, hc-sr1.GND, e-radionica1.Gnd, JACK1.NEG, Part2.GND
  VCC: J1.vcc, J2.vcc, J3.vcc, J4.vcc, hc-sr1.VCC, e-radionica1.Vcc, JACK1.POS, Part2.5V
  N1: J1.pulse, Part2.D8_PWM
  N2: J2.pulse, Part2.D9_PWM
  N3: J3.pulse, Part2.D10_PWM
  N4: J4.pulse, Part2.D11_PWM
  N5: hc-sr1.Trig, Part2.D13_PWM
  N6: hc-sr1.Echo, Part2.D12_PWM
  N7: e-radionica1.S1, Part2.D3_PWM
  N8: e-radionica1.S0, Part2.D2_PWM
  N9: e-radionica1.S3, Part2.D5_PWM
  N10: e-radionica1.S2, Part2.D4_PWM
  N11: e-radionica1.Out, Part2.D6_PWM

notes:
  base
  link1
  link 2
  claw
  5v
  2A

custom parts:
  TCS230 Color Sensor: TCS230
