# Fritzing sketch fire extinguisher (saved by Fritzing 0.9.3b)
breadboards: 1

parts:
  J2 = Basic Servo
  J3 = Basic Servo
  J4 = Basic Servo
  JACK1 = 2.1mm Barrel Jack with Terminal Block
  S1 = KY-026
  M1 = Keyes l9110 Fan module [package=THT]
  Part2 = Arduino Mega 2560 (Rev3)

nets:
  GND: J2.gnd, J3.gnd, J4.gnd, JACK1.NEG, S1.pin2, M1.pin3, Part2.GND
  VCC: J2.vcc, J3.vcc, J4.vcc, JACK1.POS, S1.pin3, M1.pin4, Part2.5V
  N1: J2.pulse, Part2.D9_PWM
  N2: J3.pulse, Part2.D10_PWM
  N3: J4.pulse, Part2.D11_PWM
  N4: S1.pin1, Part2.A0
  N5: M1.pin1, Part2.D13_PWM
  N6: M1.pin2, Part2.D12_PWM

notes:
  base
  link1
  link 2
  5v
  2A

custom parts:
  KY-026: ky-026 flame sensor module
  Keyes l9110 Fan module: Keyes l9110 Fan module. Done from pictures without an actual board to hand so breadboard may not be fully accurate.
