# Fritzing sketch gamepad control (saved by Fritzing 0.9.3b)
breadboards: 1

parts:
  J1 = Basic Servo
  J2 = Basic Servo
  J3 = Basic Servo
  J4 = Basic Servo
  JACK1 = 2.1mm Barrel Jack with Terminal Block
  Part2 = Bluetooth HC-05 Macho
  Part3 = Arduino Mega 2560 (Rev3)

nets:
  N1: J1.pulse, Part3.D8_PWM
  N2: J2.pulse, Part3.D9_PWM
  N3: J3.pulse, Part3.D10_PWM
  N4: J4.pulse, Part3.D11_PWM
  VCC: JACK1.POS, Part2.VCC, Part3.5V
  GND: JACK1.NEG, Part2.GND, Part3.GND
  N5: Part2.TXD, Part3.D0_RX0
  N6: Part2.RXD, Part3.D1_TX0

notes:
  base
  link1
  link 2
  claw
  5v
  2A
