# Fritzing sketch gyro control (saved by Fritzing 0.9.3b)
breadboards: 1

parts:
  J1 = Basic Servo
  J2 = Basic Servo
  J3 = Basic Servo
  J4 = Basic Servo
  JACK1 = 2.1mm Barrel Jack with Terminal Block
  GY1 = MPU-6050 Board GY-521 [form="♀ (female)" package=THT]
  S1 = Pushbutton [package="[SMD]"]
  S2 = Pushbutton [package="[SMD]"]
  R1 = Resistor [tolerance=±5% resistance=1k package=THT]
  R2 = Resistor [tolerance=±5% resistance=1k package=THT]
  Part2 = Arduino Mega 2560 (Rev3)

nets:
  GND: J1.gnd, J2.gnd, J3.gnd, J4.gnd, JACK1.NEG, GY1.pin2, R1.Pin_0, Part2.GND
  VCC: J1.vcc, J2.vcc, J3.vcc, J4.vcc, JACK1.POS, GY1.pin1, S1.Pin_1, S1.Pin_2, S2.Pin_1, S2.Pin_2, S2.Pin_3, S2.Pin_4, R2.Pin_0, R2.Pin_1, Part2.D13_PWM, Part2.5V
  N1: J1.pulse, Part2.D8_PWM
  N2: J2.pulse, Part2.D9_PWM
  N3: J3.pulse, Part2.D10_PWM
  N4: J4.pulse, Part2.D11_PWM
  N5: GY1.pin3, Part2.A5
  N6: GY1.pin4, Part2.A4
  N7: S1.Pin_3, S1.Pin_4, R1.Pin_1, Part2.D12_PWM

notes:
  base
  link1
  link 2
  claw
  5v
  2A

custom parts:
  MPU-6050 Board GY-521: Acelerometro y Giroscopio MPU-6050 Board GY-521
