# Fritzing sketch webcam (saved by Fritzing 0.9.3b)
breadboards: 1

parts:
  J5 = Basic Servo
  J6 = Basic Servo
  J7 = Basic Servo
  J8 = Basic Servo
  JACK2 = 2.1mm Barrel Jack with Terminal Block
  Part3 = Arduino Mega 2560 (Rev3)

nets:
  GND: J5.gnd, J6.gnd, J7.gnd, J8.gnd, JACK2.NEG
  VCC: J5.vcc, J6.vcc, J7.vcc, J8.vcc, JACK2.POS, Part3.5V
  N1: J5.pulse, Part3.D8_PWM
  N2: J6.pulse, Part3.D9_PWM
  N3: J7.pulse, Part3.D10_PWM
  N4: J8.pulse, Part3.D11_PWM

notes:
  5v
  2A
  claw
  link 2
  link1
  base
